# Fritzing sketch CameraDiagram (saved by Fritzing 0.9.3b)

parts:
  Part2 = Arduino Ethernet Shield (Rev3)
  CAMERA1 = TTL Serial JPEG Camera

nets:
  N1: Part2.D2, CAMERA1.RX
  N2: Part2.PWM_D3, CAMERA1.TX
  5V: Part2.5V, CAMERA1.5V
  GND: Part2.GND, CAMERA1.GND

custom parts:
  TTL Serial JPEG Camera: TTL Serial JPEG Camera with NTSC Out
